// Digital circuit COMPUTER.dig as structural Verilog
module COMPUTER (
  input  clk,
  input  in_2,
  input  in_3,
  input  [7:0] IN,
  input  TEST,
  input  HLT,
  input  MI,
  input  RI,
  input  RO,
  input  IO,
  input  II,
  input  AI,
  input  AO,
  input  EI,
  input  EO,
  input  SU,
  input  BI,
  input  BO,
  input  OI,
  input  CE,
  input  CO,
  input  J,
  input  FI
);

  wire add_2_c_o, AI_t, and_1_out, and_2_out, and_3_out, and_4_out, and_5_out, and_6_out, and_7_out,
       and_8_out, and_10_out, AO_t, BI_t, BO_t, C, CE_t, CLK_t, CO_t, comparator_1_eq, d_ff_as_1_q,
       d_ff_as_2_q, d_ff_as_3_q, d_ff_as_4_q, d_ff_as_5_q, d_ff_as_6_q, EI_t, EO_t, FI_t, HLT_t, II_t, IO_t,
       J_t, MI_t, not_1_out, not_2_out, not_3_out, not_4_out, not_5_out, not_6_out, not_7_out, not_8_out,
       not_9_out, not_10_out, not_11_out, OI_t, or_1_out, RI_t, RO_t, SU_t, Z;
  wire [3:0] add_1_s, d_ff_1_q, d_ff_2_q, d_ff_4_q, driver_1_out, driver_3_out, multiplexer_1_out;
  wire [6:0] d_ff_2_q_2;
  wire [7:0] add_2_s, bit_extender_1_p1, d_ff_3_q, d_ff_5_q, d_ff_6_q, d_ff_7_q, ramasync_1_q, xor_1_out;
  wire [17:0] rom_1_d;
  wire [23:0] rom_2_d;

  D_FF_AS d_ff_as_1 (.Set(in_2), .D(d_ff_as_6_q), .C(CLK_t), .Clr(1'b0), .Q(d_ff_as_1_q));  // open: nQ
  PriorityEncoder #(.Selector_Bits(3)) priorityencoder_1 (
    .in0(d_ff_as_1_q), .in1(d_ff_as_2_q), .in2(d_ff_as_3_q), .in3(d_ff_as_4_q), .in4(d_ff_as_5_q),
    .in5(d_ff_as_6_q), .in6(1'b0), .in7(1'b0), .num(d_ff_2_q_2[2:0]));  // open: any
  D_FF_AS d_ff_as_2 (.Set(1'b0), .D(d_ff_as_1_q), .C(CLK_t), .Clr(in_2), .Q(d_ff_as_2_q));  // open: nQ
  D_FF_AS d_ff_as_3 (.Set(1'b0), .D(d_ff_as_2_q), .C(CLK_t), .Clr(in_2), .Q(d_ff_as_3_q));  // open: nQ
  D_FF_AS d_ff_as_4 (.Set(1'b0), .D(d_ff_as_3_q), .C(CLK_t), .Clr(in_2), .Q(d_ff_as_4_q));  // open: nQ
  D_FF_AS d_ff_as_5 (.Set(1'b0), .D(d_ff_as_4_q), .C(CLK_t), .Clr(in_2), .Q(d_ff_as_5_q));  // open: nQ
  D_FF_AS d_ff_as_6 (.Set(1'b0), .D(d_ff_as_5_q), .C(CLK_t), .Clr(in_2), .Q(d_ff_as_6_q));  // open: nQ
  and and_1 (and_1_out, II_t, not_1_out);
  not not_1 (not_1_out, CLK_t);
  and and_2 (and_2_out, MI_t, not_2_out);
  not not_2 (not_2_out, CLK_t);
  ROM #(.AddrBits(9), .isProgramMemory("true"), .Bits(18)) rom_1 (.A({C, Z, d_ff_2_q_2}), .sel(1'b1), .D(rom_1_d));
  RAMAsync #(.AddrBits(4), .isProgramMemory("true"), .Bits(8)) ramasync_1 (
    .A(d_ff_1_q), .D({driver_3_out, driver_1_out}), .we(and_3_out), .Q(ramasync_1_q));
  D_FF #(.Bits(4)) d_ff_1 (.D(driver_1_out), .C(and_2_out), .Q(d_ff_1_q));  // open: nQ
  and and_3 (and_3_out, not_3_out, RI_t);
  not not_3 (not_3_out, CLK_t);
  D_FF #(.Bits(8)) d_ff_2 (
    .D({driver_3_out, driver_1_out}), .C(and_1_out), .Q({d_ff_2_q_2[6:3], d_ff_2_q}));  // open: nQ
  assign driver_1_out = IO_t ? d_ff_2_q : 4'bz;  // Driver driver_1
  assign {HLT_t, MI_t, RI_t, RO_t, IO_t, II_t, AI_t, AO_t, EI_t, EO_t, SU_t, BI_t, BO_t, OI_t, CE_t, CO_t, J_t, FI_t} = ~TEST ? rom_1_d : 18'bz;  // DriverInvSel driverinvsel_1
  assign {HLT_t, MI_t, RI_t, RO_t, IO_t, II_t, AI_t, AO_t, EI_t, EO_t, SU_t, BI_t, BO_t, OI_t, CE_t, CO_t, J_t, FI_t} = TEST ? {HLT, MI, RI, RO, IO, II, AI, AO, EI, EO, SU, BI, BO, OI, CE, CO, J, FI} : 18'bz;  // Driver driver_2
  assign driver_3_out = IO_t ? 4'b0000 : 4'bz;  // Driver driver_3
  assign {driver_3_out, driver_1_out} = in_3 ? IN : 8'bz;  // Driver driver_4
  assign {driver_3_out, driver_1_out} = RO_t ? ramasync_1_q : 8'bz;  // Driver driver_5
  and and_4 (and_4_out, or_1_out, not_4_out);
  not not_4 (not_4_out, CLK_t);
  assign driver_1_out = CO_t ? d_ff_4_q : 4'bz;  // Driver driver_6
  assign driver_3_out = CO_t ? 4'b0000 : 4'bz;  // Driver driver_7
  assign {driver_3_out, driver_1_out} = AO_t ? d_ff_5_q : 8'bz;  // Driver driver_8
  assign {driver_3_out, driver_1_out} = BO_t ? d_ff_7_q : 8'bz;  // Driver driver_9
  assign {driver_3_out, driver_1_out} = EO_t ? d_ff_6_q : 8'bz;  // Driver driver_10
  or or_1 (or_1_out, J_t, CE_t);
  not not_5 (not_5_out, CLK_t);
  D_FF #(.Bits(8)) d_ff_3 (.D({driver_3_out, driver_1_out}), .C(and_7_out), .Q(d_ff_3_q));  // open: nQ
  not not_6 (not_6_out, and_4_out);
  D_FF #(.Bits(4)) d_ff_4 (.D(multiplexer_1_out), .C(not_6_out), .Q(d_ff_4_q));  // open: nQ
  and and_5 (and_5_out, AI_t, not_5_out);
  not not_7 (not_7_out, CLK_t);
  Add #(.Bits(4)) add_1 (.a(d_ff_4_q), .b(4'b0001), .c_i(1'b0), .s(add_1_s));  // open: c_o
  not not_8 (not_8_out, and_5_out);
  and and_6 (and_6_out, EI_t, not_7_out);
  and and_7 (and_7_out, not_9_out, OI_t);
  ROM #(.bigEndian("true"), .AddrBits(8), .isProgramMemory("true"), .Bits(24)) rom_2 (
    .A(d_ff_3_q), .sel(1'b1), .D(rom_2_d));
  Multiplexer #(.Bits(4)) multiplexer_1 (.sel(J_t), .in_0(add_1_s), .in_1(driver_1_out), .out(multiplexer_1_out));
  D_FF #(.Bits(8)) d_ff_5 (.D({driver_3_out, driver_1_out}), .C(not_8_out), .Q(d_ff_5_q));  // open: nQ
  not not_9 (not_9_out, CLK_t);
  and and_8 (and_8_out, BI_t, CLK_t);
  Add #(.Bits(8)) add_2 (.a(d_ff_5_q), .b(xor_1_out), .c_i(SU_t), .s(add_2_s), .c_o(add_2_c_o));
  D_FF #(.Bits(8)) d_ff_6 (.D(add_2_s), .C(and_6_out), .Q(d_ff_6_q));  // open: nQ
  assign xor_1_out = bit_extender_1_p1 ^ d_ff_7_q;  // XOr xor_1, 8 bits wide
  D_FF #(.Bits(8)) d_ff_7 (.D({driver_3_out, driver_1_out}), .C(and_8_out), .Q(d_ff_7_q));  // open: nQ
  D_FF d_ff_8 (.D(add_2_c_o), .C(and_10_out), .Q(C));  // open: nQ
  Comparator #(.Bits(8)) comparator_1 (.a(add_2_s), .b({8{1'b0}}), .eq(comparator_1_eq));  // open: gt, lt
  D_FF d_ff_9 (.D(comparator_1_eq), .C(and_10_out), .Q(Z));  // open: nQ
  not not_10 (not_10_out, HLT_t);
  Seven_Seg seven_seg_1 (
    .a(rom_2_d[16]), .b(rom_2_d[17]), .c(rom_2_d[18]), .d(rom_2_d[19]), .e(rom_2_d[20]), .f(rom_2_d[21]),
    .g(rom_2_d[22]), .dp(rom_2_d[23]));
  // bit_extender bit_extender_1: pin names not known; wires that end beside it: bit_extender_1_p1, SU_t
  and and_9 (CLK_t, clk, not_10_out);
  Seven_Seg seven_seg_2 (
    .a(rom_2_d[8]), .b(rom_2_d[9]), .c(rom_2_d[10]), .d(rom_2_d[11]), .e(rom_2_d[12]), .f(rom_2_d[13]),
    .g(rom_2_d[14]), .dp(rom_2_d[15]));
  Seven_Seg seven_seg_3 (
    .a(rom_2_d[0]), .b(rom_2_d[1]), .c(rom_2_d[2]), .d(rom_2_d[3]), .e(rom_2_d[4]), .f(rom_2_d[5]),
    .g(rom_2_d[6]), .dp(rom_2_d[7]));
  and and_10 (and_10_out, not_11_out, FI_t);
  not not_11 (not_11_out, CLK_t);

  // Other names for the same wires on the sheet: RST = in_2; TI = in_3

  // Notes on the sheet:
  //   clk: Hz: 30
  //   rom_1 loads control_unit.hex
  //   contents of ramasync_1 (hex, n*v repeats v):
  //   84
  //   79
  //   83
  //   47
  //   224
  //   240
  //   0
  //   0
  //   0
  //   0
  //   0
  //   0
  //   0
  //   0
  //   0
  //   0
  //   rom_2 loads rom_7seg_24bit.hex
endmodule
